// Digital circuit control_unit.dig as structural Verilog
module control_unit (
  input  [15:0] INST,
  input  ZERO,
  output [1:0] ALUOP,
  output [2:0] RS1,
  output [2:0] RS2,
  output [2:0] WS,
  output STR,
  output WE,
  output [1:0] DMUX,
  output LDR,
  output FLEN,
  output EXEC,
  output SETH
);

  wire and_2_out, and_3_out, and_4_out, and_5_out, and_6_out, and_7_out, nor_1_out, nor_2_out, nor_3_out,
       nor_4_out, not_1_out, not_2_out, or_2_out;
  wire [1:0] multiplexer_1_out, multiplexer_2_out, multiplexer_3_out, multiplexer_4_out;

  not not_1 (not_1_out, INST[11]);
  or or_1 (EXEC, ZERO, not_1_out);
  nor nor_1 (nor_1_out, INST[12], INST[14], INST[15]);
  nor nor_2 (nor_2_out, INST[12], INST[13], INST[15]);
  nor nor_3 (nor_3_out, INST[13], INST[12]);
  nor nor_4 (nor_4_out, INST[12], INST[13], INST[14], INST[15]);
  and and_1 (SETH, INST[13], nor_1_out);
  and and_2 (and_2_out, INST[14], nor_2_out);
  and and_3 (and_3_out, ~INST[15], INST[12], INST[13], INST[14]);  // And
  and and_4 (and_4_out, INST[15], nor_3_out);
  and and_5 (and_5_out, INST[12], ~INST[13], INST[15]);  // And
  and and_6 (and_6_out, ~INST[12], INST[13], INST[15]);  // And
  and and_7 (and_7_out, INST[12], INST[13], INST[15]);
  or or_2 (or_2_out, and_4_out, and_5_out, and_6_out, and_7_out);
  Multiplexer #(.Bits(2)) multiplexer_1 (.sel(nor_4_out), .in_0(2'b00), .in_1(2'b11), .out(multiplexer_1_out));
  Multiplexer #(.Bits(2)) multiplexer_2 (.sel(SETH), .in_0(2'b00), .in_1(2'b11), .out(multiplexer_2_out));
  Multiplexer #(.Bits(2)) multiplexer_3 (.sel(and_2_out), .in_0(2'b00), .in_1(2'b10), .out(multiplexer_3_out));
  Multiplexer #(.Bits(2)) multiplexer_4 (.sel(or_2_out), .in_0(2'b00), .in_1(2'b01), .out(multiplexer_4_out));
  Multiplexer #(.Bits(3)) multiplexer_5 (.sel(SETH), .in_0(INST[6:4]), .in_1(INST[10:8]), .out(RS1));
  Multiplexer #(.Bits(3)) multiplexer_6 (.sel(not_2_out), .in_0(INST[10:8]), .in_1(INST[2:0]), .out(RS2));
  not not_2 (not_2_out, and_3_out);
  and and_8 (WE, not_2_out, EXEC);
  and and_9 (STR, and_3_out, EXEC);
  and and_10 (FLEN, INST[15], EXEC);
  assign DMUX = multiplexer_1_out | multiplexer_2_out | multiplexer_3_out | multiplexer_4_out;  // Or or_3, 2 bits wide

  assign ALUOP = INST[13:12];
  assign LDR = EXEC;
  assign WS = INST[10:8];

  // Notes on the sheet:
  //   opcode
  //   Rd
  //   Ra
  //   Rb
  //   Z
  //   ALU Instructions
  //   MOVL (0000)
  //   SETH (0010)
  //   LDR (0100)
  //   STR (0111)
  //   AND (1X00)
  //   ORR (1X01)
  //   ADD (1X10)
  //   SUB (1X11)
  //   DMUX Converters
  //   ADDITIONAL TESTS
endmodule

/* Test case All Tests:
	INST                                    WE  ALUOP  RS1   RS2  WS  STR  LDR DMUX  FLEN

let aluop  = 0b1000;
let ldrop  = 0b0100;
let strop  = 0b0111;
let movlop = 0b0000;

loop(rd, 1<<3)
loop(ra, 1<<3)
loop(rb, 1<<3)

loop(i, 4)
	((aluop+i)<<12 | rd<<8 | ra<<4 | rb<<0) 1  (i)     (ra)  (rb) (rd)  0   X    1    1     #test add/sub/and/orr
end loop

	(ldrop    <<12 | rd<<8 | ra<<4 )        1  X       (ra)  x    (rd)  0   1    2    0     #test ldr
	(strop    <<12 | rd<<8 | ra<<4 )        0  X       (ra)  (rd)  X    1   X    X    0     #test str
	
	let imm = random(256);
	(movlop   <<12 | rd<<8 | imm )          1  X       X      X   (rd)  0   X    3    0     #test movl

end loop
end loop
end loop
*/

/* Test case WS:
	INST                                    WS 

let aluop  = 0b1000;
let ldrop  = 0b0100;
let strop  = 0b0111;
let movlop = 0b0000;

loop(rd, 1<<3)
loop(ra, 1<<3)
loop(rb, 1<<3)

loop(i, 4)
	((aluop+i)<<12 | rd<<8 | ra<<4 | rb<<0) (rd)  #test add/sub/and/orr
end loop

	(ldrop    <<12 | rd<<8 | ra<<4 )        (rd)   #test ldr
	(strop    <<12 | rd<<8 | ra<<4 )        X     #test str
	
	let imm = random(256);
	(movlop   <<12 | rd<<8 | imm )          (rd)  #test movl

end loop
end loop
end loop
*/

/* Test case RS1:
	INST                                    RS1  

let aluop  = 0b1000;
let ldrop  = 0b0100;
let strop  = 0b0111;
let movlop = 0b0000;

loop(rd, 1<<3)
loop(ra, 1<<3)
loop(rb, 1<<3)

loop(i, 4)
	((aluop+i)<<12 | rd<<8 | ra<<4 | rb<<0) (ra)  #test add/sub/and/orr
end loop

	(ldrop    <<12 | rd<<8 | ra<<4 )        (ra)  #test ldr
	(strop    <<12 | rd<<8 | ra<<4 )        (ra)  #test str

end loop
end loop
end loop
*/

/* Test case RS2:
	INST                                    RS2  

let aluop  = 0b1000;
let ldrop  = 0b0100;
let strop  = 0b0111;
let movlop = 0b0000;

loop(rd, 1<<3)
loop(ra, 1<<3)
loop(rb, 1<<3)

loop(i, 4)
	((aluop+i)<<12 | rd<<8 | ra<<4 | rb<<0) (rb) #test add/sub/and/orr
end loop
	(strop    <<12 | rd<<8 | ra<<4 )        (rd) #test str

end loop
end loop
end loop
*/

/* Test case STR:
	INST                                    STR 

let aluop  = 0b1000;
let ldrop  = 0b0100;
let strop  = 0b0111;
let movlop = 0b0000;

loop(rd, 1<<3)
loop(ra, 1<<3)
loop(rb, 1<<3)

loop(i, 4)
	((aluop+i)<<12 | rd<<8 | ra<<4 | rb<<0) 0  #test add/sub/and/orr
end loop

	(ldrop    <<12 | rd<<8 | ra<<4 )        0  #test ldr
	(strop    <<12 | rd<<8 | ra<<4 )        1  #test str
	
	let imm = random(256);
	(movlop   <<12 | rd<<8 | imm )          0  #test movl

end loop
end loop
end loop
*/

/* Test case WE:
	INST                                    WE  

let aluop  = 0b1000;
let ldrop  = 0b0100;
let strop  = 0b0111;
let movlop = 0b0000;

loop(rd, 1<<3)
loop(ra, 1<<3)
loop(rb, 1<<3)

loop(i, 4)
	((aluop+i)<<12 | rd<<8 | ra<<4 | rb<<0) 1  #test add/sub/and/orr
end loop

	(ldrop    <<12 | rd<<8 | ra<<4 )        1  #test ldr
	(strop    <<12 | rd<<8 | ra<<4 )        0  #test str
	
	let imm = random(256);
	(movlop   <<12 | rd<<8 | imm )          1  #test movl

end loop
end loop
end loop
*/

/* Test case LDR:
	INST                                    LDR 

let aluop  = 0b1000;
let ldrop  = 0b0100;
let strop  = 0b0111;
let movlop = 0b0000;

loop(rd, 1<<3)
loop(ra, 1<<3)
loop(rb, 1<<3)

loop(i, 4)
	((aluop+i)<<12 | rd<<8 | ra<<4 | rb<<0) X    #test add/sub/and/orr
end loop

	(ldrop    <<12 | rd<<8 | ra<<4 )        1    #test ldr
	(strop    <<12 | rd<<8 | ra<<4 )        X    #test str
	
	let imm = random(256);
	(movlop   <<12 | rd<<8 | imm )          X    #test movl

end loop
end loop
end loop
*/

/* Test case DMUX:
	INST                                    DMUX

let aluop  = 0b1000;
let ldrop  = 0b0100;
let strop  = 0b0111;
let movlop = 0b0000;

loop(rd, 1<<3)
loop(ra, 1<<3)
loop(rb, 1<<3)

loop(i, 4)
	((aluop+i)<<12 | rd<<8 | ra<<4 | rb<<0) 1  #test add/sub/and/orr
end loop

	(ldrop    <<12 | rd<<8 | ra<<4 )        2  #test ldr
	
	let imm = random(256);
	(movlop   <<12 | rd<<8 | imm )          3  #test movl

end loop
end loop
end loop
*/

/* Test case ALUOP:
	INST                                    ALUOP 

let aluop  = 0b1000;
let ldrop  = 0b0100;
let strop  = 0b0111;
let movlop = 0b0000;

loop(rd, 1<<3)
loop(ra, 1<<3)
loop(rb, 1<<3)

loop(i, 4)
	((aluop+i)<<12 | rd<<8 | ra<<4 | rb<<0) (i)    #test add/sub/and/orr
end loop

end loop
end loop
end loop
*/

/* Test case FLEN:
	INST                                    FLEN 

let aluop  = 0b1000;
let ldrop  = 0b0100;
let strop  = 0b0111;
let movlop = 0b0000;

loop(rd, 1<<3)
loop(ra, 1<<3)
loop(rb, 1<<3)

loop(i, 4)
	((aluop+i)<<12 | rd<<8 | ra<<4 | rb<<0) (1)    #test add/sub/and/orr
end loop
        (ldrop<<12 | rd<<8 | ra<<4 | 0b0000)    (0)    #test ldr
        (strop<<12 | rd<<8 | ra<<4 | 0b0000)    (0)    #test ldr

end loop
end loop
end loop
*/

/* Test case SETH:
	INST                              SETH 
let aluop  = 0b1000;
let ldrop  = 0b0100;
let strop  = 0b0111;
let movlop = 0b0000;

loop(rd, 1<<3)
loop(ra, 1<<3)
loop(rb, 1<<3)
	#SETH should only be set to true when opcode = 1
	(0<<12| rd<<8 | ra<<4 | rb<<0)    (0) 
	(1<<12| rd<<8 | ra<<4 | rb<<0)    (0) 
	(2<<12| rd<<8 | ra<<4 | rb<<0)    (1) 
loop(i, 13)
	((i+3)<<12|rd<<8 | ra<<4 | rb<<0) (0) 
end loop
end loop
end loop
end loop
*/

/* Test case EXEC:
	INST		ZERO	EXEC
loop(o, 16)
loop(x, 1024)
	(o<<12|0<<11|x)	(0)	(1)
	(o<<12|0<<11|x)	(1)	(1)
	(o<<12|1<<11|x)	(0)	(0)
	(o<<12|1<<11|x)	(1)	(1)
end loop
end loop
*/
