// Digital circuit extended-cpu.dig as structural Verilog
module extended_cpu (
  input  CLK
);

  wire ALUIM, and_1_out, CALL, CALREG, extended_cu_1_exec, extended_cu_1_setc, FLEN, ld, MEMIM,
       multiplexer_4_out, PSTO, SETH, STR, WE, WE2;
  wire [1:0] ALUOP, COND_q, DMUX;
  wire [2:0] multiplexer_5_out, R3, RS1, RS2, WS;
  wire [3:0] alu_1_flag;
  wire [7:0] extended_regfile_1_out1;
  wire [15:0] alu_1_result, extended_regfile_1_fl, extended_regfile_1_out2, extended_regfile_1_out3,
       extended_regfile_1_pc, extended_regfile_1_pc_plus_1, IMM, multiplexer_1_out, multiplexer_2_out,
       multiplexer_3_out, multiplexer_6_out, multiplexer_7_out, multiplexer_8_out, multiplexer_9_out,
       multiplexer_10_out, multiplexer_11_out, notconnected_1_out, RAM_d1, RAM_d2;
  wire [15:8] extended_regfile_1_out1_2;

  Multiplexer #(.Selector_Bits(2), .Bits(16)) multiplexer_1 (
    .sel(DMUX), .in_0(notconnected_1_out), .in_1(alu_1_result), .in_2(multiplexer_6_out),
    .in_3(multiplexer_2_out), .out(multiplexer_1_out));
  // NotConnected on notconnected_1_out
  Multiplexer #(.Bits(16)) multiplexer_2 (
    .sel(SETH), .in_0(multiplexer_3_out), .in_1({RAM_d2[7:0], extended_regfile_1_out1}),
    .out(multiplexer_2_out));
  Multiplexer #(.Bits(16)) multiplexer_3 (
    .sel(CALREG), .in_0(IMM), .in_1(extended_regfile_1_out3), .out(multiplexer_3_out));
  // Probe DATA on multiplexer_1_out
  extended_cu extended_cu_1 (
    .INST(RAM_d2), .COND(multiplexer_4_out), .RS1(RS1), .RS2(RS2), .WS(WS), .STR(STR), .WE(WE), .DMUX(DMUX),
    .LDR(ld), .SETH(SETH), .RS3(R3), .IMM(IMM), .PSTO(PSTO), .FLEN(FLEN), .ALUOP(ALUOP), .WE2(WE2),
    .MEMIM(MEMIM), .CALREG(CALREG), .CALL(CALL), .ALUIM(ALUIM), .EXEC(extended_cu_1_exec),
    .SETC(extended_cu_1_setc));
  LED led_1 (.in(extended_cu_1_exec));
  Register #(.Bits(2)) COND (.D(WS[1:0]), .C(CLK), .en(extended_cu_1_setc), .Q(COND_q));
  Multiplexer #(.Selector_Bits(2)) multiplexer_4 (
    .sel(COND_q), .in_0(extended_regfile_1_fl[0]), .in_1(extended_regfile_1_fl[1]),
    .in_2(extended_regfile_1_fl[2]), .in_3(extended_regfile_1_fl[3]), .out(multiplexer_4_out));
  Multiplexer #(.Bits(3)) multiplexer_5 (.sel(CALL), .in_0(RS1), .in_1(3'b110), .out(multiplexer_5_out));
  extended_regfile extended_regfile_1 (
    .RS1(RS1), .RS2(RS2), .WE1(WE), .IN1(multiplexer_1_out), .clk(CLK), .WS1(WS), .RS3(R3),
    .WS2(multiplexer_5_out), .IN2(alu_1_result), .PRI(1'b1), .WE2(WE2), .FLD(alu_1_flag), .FLEN(FLEN),
    .OUT1({extended_regfile_1_out1_2, extended_regfile_1_out1}), .OUT2(extended_regfile_1_out2),
    .PC(extended_regfile_1_pc), .OUT3(extended_regfile_1_out3), .PC_plus_1(extended_regfile_1_pc_plus_1),
    .FL(extended_regfile_1_fl));
  and and_1 (and_1_out, RS1[0], RS1[1], RS1[2], ~MEMIM);  // And
  Multiplexer #(.Bits(16)) multiplexer_6 (
    .sel(and_1_out), .in_0(RAM_d1), .in_1(extended_regfile_1_fl), .out(multiplexer_6_out));
  Multiplexer #(.Bits(16)) multiplexer_7 (
    .sel(CALL), .in_0(extended_regfile_1_out3), .in_1({16{1'b1}}), .out(multiplexer_7_out));
  Multiplexer #(.Bits(16)) multiplexer_8 (.sel(ALUIM), .in_0(multiplexer_7_out), .in_1(IMM), .out(multiplexer_8_out));
  alu alu_1 (
    .A({extended_regfile_1_out1_2, extended_regfile_1_out1}), .B(multiplexer_8_out), .ALUOP(ALUOP),
    .RESULT(alu_1_result), .FLAG(alu_1_flag));
  Multiplexer #(.Bits(16)) multiplexer_9 (.sel(MEMIM), .in_0(alu_1_result), .in_1(IMM), .out(multiplexer_9_out));
  Multiplexer #(.Bits(16)) multiplexer_10 (
    .sel(PSTO), .in_0(multiplexer_9_out), .in_1({extended_regfile_1_out1_2, extended_regfile_1_out1}),
    .out(multiplexer_10_out));
  Multiplexer #(.Bits(16)) multiplexer_11 (
    .sel(CALL), .in_0(extended_regfile_1_out2), .in_1(extended_regfile_1_pc_plus_1), .out(multiplexer_11_out));
  RAMDualAccess #(.AddrBits(16), .isProgramMemory("true"), .Bits(16)) RAM (
    .str(STR), .C(CLK), .ld(ld), .A1(multiplexer_10_out), .Din1(multiplexer_11_out),
    .A2(extended_regfile_1_pc), .D1(RAM_d1), .D2(RAM_d2));

  // Notes on the sheet:
  //   Assembly tests converted to Digital
  //   Integration Tests
  //   UNIT TESTS FOR EACH EXTENSION
  //   (Except Pre/Post LDR/STR, these tests
  //   are not converted to digital tests, but they
  //   can be found in the unit tests folder)
  //   DMUX
  //   Checks FL reg
  //   INST
  //   SETH Logic
  //   Address Bus
endmodule

/* Test case CHECK:
# assert these registers can be tested
CLK R1 R2 R3 R4 FL PC

program(0)  # assert program memory exists
init R1=0;  # assert we can initialise R1
init R2=0;  # assert we can initialise R2
init R3=0;  # assert we can initialise R3
init R4=0;  # assert we can initialise R4
init PC=0;  # assert we can initialise PC
init FL=0;  # assert we can initialise FL

0 0 0 0 0 0 0
*/

/* Test case MOVL:
CLK     R1     R2     R3     R4     PC

0        x      x      x      x 0x0000
c   0x0012      x      x      x 0x0001
c   0x0012 0x0034      x      x 0x0002
c   0x0012 0x0034 0x0056      x 0x0003
c   0x0012 0x0034 0x0056 0x0078 0x0004
c   0x0000 0x0034 0x0056 0x0078 0x0005
c   0x0000 0x0001 0x0056 0x0078 0x0006

program(0x0112,0x0234,0x0356,0x0478,0x0100,0x0201)
*/

/* Test case AND/ORR:
CLK     R1     R2     R3     R4     PC

init R2=0x5a96;
init R3=0x5849;
init R4=0xa569;

0        x      x      x      x 0x0000
c   0xFFFF      x      x      x 0x0001
c   0xFFFF 0x5800      x      x 0x0002
c   0xFFFF 0x5800 0x0049      x 0x0003
c   0xFFFF 0x5800 0x0049 0xFFFF 0x0004
c   0x0000 0x5800 0x0049 0xFFFF 0x0005
c   0x0000 0x5800 0x0049 0xFFFF 0x0006

program(0x9124,0x8232,0x8343,0x9410,0x8123,0x9333)
*/

/* Test case ADD/SUB:
CLK     R1     R2     R3     R4     PC

init R1=0x1234;
init R2=0xABCD;
init R3=0xFFFF;

0        x      x      x      x 0x0000
c        x      x      x 0xBE01 0x0001
c        x      x      x 0xBE01 0x0002
c        x      x      x 0xBE02 0x0003
c        x      x      x 0xABCE 0x0004
c        x      x      x 0x0001 0x0005
c        x      x      0 0x0001 0x0006

program(0xa412,0xa440,0xb443,0xb441,0xb442,0xa343)
*/

/* Test case LDR/STR:
CLK     R1     R2     R3     R4     PC

init R1=0x6;
init R4=0x7;

0        x      x      x      x 0x0000
c        x 0x4200      x      x 0x0001
c        x 0x4200      x      x 0x0002
c        x 0x4200 0x0005      x 0x0003
c   0x4410 0x4200 0x0005      x 0x0004
c   0x4410 0x4200 0x0005      x 0x0005
c   0x4410 0x4200 0x0005 0x4200 0x0006
c   0x4410 0x4200 0x0005 0x4200 0x0007

program(0x4200,0x7210,0x4340,0x4130,0x7210,0x4410,0x0001,0x0005)
*/

/* Test case ALU:
CLK     R1     R2     R3     R4   FLAGS     PC

declare FLAGS = FL & 0xF;

init R1=0x1A;
init R2=0xCDFF;
init R3=0x0;

0        x      x      x      x      x 0x0000
c   0x001a 0xcdff      x 0xce19 0x0002 0x0001
c   0x001a 0xcdff      x 0x001a 0x0000 0x0002
c   0x001a 0xcdff      x 0xcdff 0x000A 0x0003
c   0x001a 0xcdff      x 0x3201 0x0000 0x0004
c   0x001a 0xcdff      x 0x0000 0x0001 0x0005
c   0x001a 0xcdff      x 0x0000 0x0001 0x0006
c   0x001a 0xcdff      x 0xcdff 0x0002 0x0007
c   0x001a 0xcdff      x 0xcdff 0x0002 0x0008
c   0x0000 0xcdff      x 0xcdff 0x0001 0x0009
c   0x0000 0x0000      x 0xcdff 0x0001 0x000a

program(0xa412, 0x8421, 0xb423, 0xb432, 0x8413, 0x8431, 0x9412, 0x9012, 0xa100, 0xa230)
*/

/* Test case FIB_20:
# This test calculates the 20th fibonacci number
# which should be 6765 = 0x1A6D. Refer to fib.quac
# in the assignment repo for the assembly code.

	CLK	R4

loop(i, 226)
	c	x	#Don't care about intermediate steps
end loop

	c	6765	#Result of fibonacci number calculation

program(0x0000, 0x2201, 0x0114, 0x0000, 0x0000, 0x3101, 0x1014, 0x44AF, 0x0532, 0x0000, 0x43AF, 0x44AE, 0xA443, 0x7420, 0xB5E1, 0x0000, 0x0000, 0x0000, 0x0000, 0x0000, 0x90A1, 0xF101, 0xBDE1, 0x0301, 0x93A1, 0xF101, 0xBDE1, 0x030A, 0x3300, 0xE201, 0x0519, 0x0000)
*/

/* Test case ALUIM:
# This tests ALU immediate operations. R1 tests add, R2 tests sub, R3 tests AND, R4 tests ORR
# Assembly: unit_tests/aluim.quac
	CLK	R1	R2	R3	R4

loop(i, 55)
	c	x	x	x	x	#Don't care about intermediate steps
end loop

	c	(210)	(21)	(58)	(241)

program(0x0000, 0x0000, 0xE101, 0xE102, 0xE103, 0xE104, 0xE105, 0xE106, 0xE107, 0xE108, 0xE109, 0xE10A, 0xE10B, 0xE10C, 0xE10D, 0xE10E, 0xE10F, 0xE110, 0xE111, 0xE112, 0xE113, 0xE114, 0x02D2, 0xF214, 0xF213, 0xF212, 0xF211, 0xF210, 0xF20F, 0xF20E, 0xF20D, 0xF20C, 0xF20B, 0xF20A, 0xF209, 0xF208, 0xF207, 0x03FF, 0xC3FF, 0xC3FB, 0xC3BF, 0xC3BB, 0xC3FF, 0xC3FE, 0xC37F, 0x0000, 0xD400, 0xD401, 0xD481, 0xD410, 0xD420, 0xD401, 0xD440, 0x0000, 0x0000, 0x0000, 0x0000, 0x0000, 0x0000, 0x0000, 0x0000, 0x0000, 0x0000, 0x0000)
*/

/* Test case SETC:
# This tests SETC.
# Assembly: unit_tests/setc.quac
	CLK	R1	R2	R3	R4

loop(i, 30)
	c	x	x	x	x	#Don't care about intermediate steps
end loop
	c	(0)	(50)	(60)	(0)

program(0x0000, 0x3101, 0xE000, 0x09FF, 0xF005, 0x09FF, 0x3201, 0x0900, 0x3301, 0x0900, 0x3001, 0x0900, 0x3101, 0x0900, 0x3001, 0xE000, 0x09FF, 0x3301, 0x0101, 0x2141, 0xA111, 0x0100, 0x3001, 0x0A32, 0x3101, 0x0A32, 0x3201, 0x0B3C, 0x3301, 0x0A46, 0x0000, 0x0000)
*/

/* Test case FLAGS:
CLK     R1     R2     R3     R4   FLAGS     PC

declare FLAGS = FL & 0xF;

init R1=1;
init R2=0xFFFF;
init R3=0x7FFF;
init R4=0x8000;
0        x      x      x      x      x 0x0000
c   0x0001 0xffff 0x7fff 0x8000 0x0001 0x0001
c   0x0001 0xffff 0x7fff 0x8000 0x0009 0x0002
c   0x0001 0xffff 0x7fff 0x8000 0x0009 0x0003
c   0x0001 0xffff 0x7fff 0x8000 0x0000 0x0004
c   0x0001 0xffff 0x7fff 0x8000 0x000A 0x0005
c   0x0001 0xffff 0x7fff 0x8000 0x000A 0x0006
c   0x0001 0xffff 0x7fff 0x8000 0x0002 0x0007
c   0x0001 0xffff 0x7fff 0x8000 0x0002 0x0008
c   0x0001 0xffff 0x7fff 0x8000 0x000c 0x0009
c   0x0001 0xffff 0x7fff 0x8000 0x0008 0x000a
c   0x0001 0xffff 0x7fff 0x8000 0x000c 0x000b
c   0x0001 0xffff 0x7fff 0x8000 0x0006 0x000c

program(0xa000, 0xa012, 0xb011, 0xb012, 0xa022, 0xb021, 0xa034, 0xa041, 0xb041, 0xb031, 0xb043, 0xa013)
*/

/* Test case READ_FLAGS:
CLK     R1     R2     R3     R4     PC

init R1=0x76;
init R4=0xF;
0        x      x      x      x 0x0000
c   0x0076 0x0000      x 0x000f 0x0001
c   0x0076 0x0000      x 0x000f 0x0002
c   0x0076 0x0000 0x0009 0x000f 0x0003

program(0xb211, 0xa370, 0x8334)
*/

/* Test case COND:
CLK     R1     R2     R3     R4     PC

0        x      x      x      x 0x0000
c   0x0000      x      x      x 0x0001
c   0x0000 0x0000      x      x 0x0002
c   0x0000 0x0000 0x0016      x 0x0003
c   0x0000 0x0000 0x0016 0x0001 0x0004
c   0x0000 0x0000 0x0016 0x0001 0x0005
c   0x0000 0x0001 0x0016 0x0001 0x0006
c   0x0000 0x0001 0x0016 0x0001 0x0007
c   0x0000 0x0001 0x0016 0x0001 0x0008
c   0x0000 0x0001 0x0016 0x0001 0x0009
c   0x0000 0x0001 0x0016 0x0001 0x000a
c   0x1337 0x0001 0x0016 0x0001 0x000b
c   0x1337 0x0001 0x0017 0x0001 0x000c
c   0x1337 0x0001 0x0017 0x0001 0x000d
c   0x1337 0x0000 0x0017 0x0001 0x000e
c   0x1337 0x0000 0x0017 0x0001 0x000f
c   0x1337 0x0000 0x0017 0x0001 0x0010
c   0x1337 0x1337 0x0017 0x0001 0x0011
c   0x1337 0x1337 0x0017 0x0001 0x0012
c   0x1337 0x1337 0x0017 0x0001 0x0013
c   0x1337 0x1337 0x0017 0x0001 0x0014
c   0x0051 0x1337 0x0017 0x0001 0x0015

program(0x0100, 0x0200, 0x0316, 0x0401, 0xa000, 0xaa04, 0x9944, 0xb040, 0x4930, 0xb000, 0x4930, 0xa334, 0x7930, 0x4230, 0xb000, 0x7930, 0x4230, 0xb040, 0x0915, 0xb000, 0x0951, 0x0000, 0x1337)
*/

/* Test case GP_PC:
CLK     R1     R2     R3     R4     PC

init R1=0x5;
init R2=0x98;
0        x      x      x      x 0x0000
c   0x0005 0x0098      x      x 0x0001
c   0x0005 0x0098      x      x 0x0002
c   0x0005 0x0002      x      x 0x0003
c   0x0005 0x0002      x      x 0x0005

program(0xa000,0xa000,0xa250,0xa510,0x03ff,0x0000)
*/

/* Test case COND_PC:
CLK     R1     R2     R3     R4     PC

0        x      x      x      x 0x0000
c   0x00FF      x      x      x 0x0001
c   0x00FF 0x00FE      x      x 0x0002
c   0x00FF 0x00FE 0xFFFF      x 0x0003
c   0x00FF 0x00FE 0xFFFF      x 0x0004
c   0x00FF 0x0002 0xFFFF      x 0x0005
c   0x00FF 0x0002 0xFFFF      x 0x0006
c   0x00FF 0x0002 0xFFFF      x 0x0008


program(0x01ff,0x02fe,0xb321,0x0d01,0x0202,0xb433,0xad52,0x0500,0x0112)
*/

/* Test case FACTORIAL_7:
# This test calculates 7! = 5040.

	CLK	R4

loop(i, 5514)
	c	x	#Don't care about intermediate steps
end loop

	c	5040	#Result of factorial

program(0x0107, 0x61F0, 0x2210, 0x0301, 0x7320, 0x102D, 0x053B, 0x0000, 0x0000, 0x0000, 0x0000, 0x0000, 0x0000, 0x0000, 0x0000, 0x0400, 0x51F1, 0x53F2, 0xA010, 0x6CF3, 0xBDE1, 0xA443, 0xF101, 0xF505, 0x0000, 0x0000, 0x0000, 0x0000, 0x0000, 0x4120, 0x61F1, 0x0300, 0x2310, 0xB323, 0xE301, 0x63F2, 0x100F, 0x51F3, 0x81A1, 0xB5E1, 0x0000, 0x0000, 0x0000, 0x0000, 0x0000, 0x0100, 0x2110, 0xB121, 0x53F0, 0xB031, 0x4C20, 0x6CF4, 0xBDE1, 0x101D, 0xF509, 0x0000, 0x0000, 0x0000, 0x0000, 0x0000, 0x0000, 0x0000, 0x0000, 0x0000)
*/

/* Test case MEMIM:
# This tests memory immediate operations.
# Assembly: unit_tests/memim.quac
	CLK	R1	R2	R3	R4

loop(i, 16)
	c	x	x	x	x	#Don't care about intermediate steps
end loop

	c	(200)	(100)	(0xAD)	(0xDE)

program(0x0000, 0x0000, 0x0000, 0x01DE, 0x02AD, 0x61FE, 0x62FF, 0x53FF, 0x54FE, 0x0164, 0x02C8, 0x6101, 0x6202, 0x5201, 0x5102, 0x0000)
*/

/* Test case MULT_11x13 (Function Calls):
# This test multiplies 11 by 13 by repeated addition. 11 x 13 = 143,
# so the result of R4 at the end should be 143.

	CLK	R4

loop(i, 86)
	c	x	#Don't care about intermediate steps
end loop

	c	0x008F	#Result of multiplication

program(0x100B, 0x0515, 0xA442, 0xF301, 0xB5E1, 0x0000, 0x0000, 0x1002, 0xBDE1, 0x0507, 0x0000, 0x0000, 0x5213, 0x5314, 0x1006, 0xB5E1, 0x0000, 0x0000, 0x0000, 0x000B, 0x000D, 0x0200, 0x0000, 0x0000, 0x0000, 0x0000, 0x0000, 0x0000, 0x0000, 0x0000, 0x0000, 0x0000)
*/

/* Test case PUSH POP:
# This tests PUSH and POP operation.
# Assembly: unit_tests/stack.quac
	CLK	R1	R2	R3	R4

loop(i, 21)
	c	x	x	x	x	#Don't care about intermediate steps
end loop
	c	(0xE9)	(0xCA)	(0xAB)	(1)

program(0x0000, 0x0000, 0x0000, 0x0101, 0x02AB, 0x03DE, 0x0423, 0x81EF, 0x82EF, 0x83EF, 0x84EF, 0xB0E1, 0xB0E1, 0x01CA, 0x02E9, 0x81EF, 0x82EF, 0xB1E1, 0xB2E1, 0xB3E1, 0xB4E1, 0x0000, 0x0000, 0x0000, 0x0000, 0x0000, 0x0000, 0x0000, 0x0000, 0x0000, 0x0000, 0x0000)
*/

/* Test case LOOP:
CLK     R1     R2     R3     R4     PC

init R2=1;
init R4=0x5512;

0        x      x      x      x 0x0000
c        x      1 0x5511 0x5512 0x0001
c   0x0000      1 0x5511 0x5510 0x0002
c   0x0001      1 0x5511 0x5510 0x0003
c   0x0001      1 0x5511 0x5510 0x0004
c   0x0001      1 0x5511 0x5510 0x0005

c   0x0001      1 0x5511 0x5510 0x0000
c   0x0001      1 0x550F 0x5510 0x0001
c   0x0001      1 0x550F 0x5500 0x0002
c   0x0002      1 0x550F 0x5500 0x0003
c   0x0002      1 0x550F 0x5500 0x0004
c   0x0002      1 0x550F 0x5500 0x0005

c   0x0002      1 0x550F 0x5500 0x0000
c   0x0002      1 0x54FF 0x5500 0x0001
c   0x0002      1 0x54FF 0x5400 0x0002
c   0x0003      1 0x54FF 0x5400 0x0003
c   0x0003      1 0x54FF 0x5400 0x0004
c   0x0003      1 0x54FF 0x5400 0x0005

c   0x0003      1 0x54FF 0x5400 0x0000
c   0x0003      1 0x53FF 0x5400 0x0001
c   0x0003      1 0x53FF 0x5000 0x0002
c   0x0004      1 0x53FF 0x5000 0x0003
c   0x0004      1 0x53FF 0x5000 0x0004
c   0x0004      1 0x53FF 0x5000 0x0005

c   0x0004      1 0x53FF 0x5000 0x0000
c   0x0004      1 0x4FFF 0x5000 0x0001
c   0x0004      1 0x4FFF 0x4000 0x0002
c   0x0005      1 0x4FFF 0x4000 0x0003
c   0x0005      1 0x4FFF 0x4000 0x0004
c   0x0005      1 0x4FFF 0x4000 0x0005

c   0x0005      1 0x4FFF 0x4000 0x0000
c   0x0005      1 0x3FFF 0x4000 0x0001
c   0x0005      1 0x3FFF 0x0000 0x0002
c   0x0006      1 0x3FFF 0x0000 0x0003
c   0x0006      1 0x3FFF 0x0000 0x0004
c   0x0006      1 0x3FFF 0x0000 0x0006
c   0x0006      1 0x3FFF 0x0006 0x0007
c   0x0000      1 0x3FFF 0x0006 0x0008
c   0x0000      1 0x3FFF 0x0006 0x0009
c   0x0000      1 0x3FFF 0x0006 0x000A
c   0x0000      1 0x3FFF 0x0006 0x000B
c   0x0000      1 0x3FFF 0x0006 0x0000
c   0x0000      1 0x0005 0x0006 0x0001
c   0x0000      1 0x0005 0x0004 0x0002
c   0x0001      1 0x0005 0x0004 0x0003
c   0x0001      1 0x0005 0x0004 0x0004
c   0x0001      1 0x0005 0x0004 0x0005
c   0x0001      1 0x0005 0x0004 0x0000
c   0x0001      1 0x0003 0x0004 0x0001
c   0x0001      1 0x0003 0x0000 0x0002
c   0x0002      1 0x0003 0x0000 0x0003
c   0x0002      1 0x0003 0x0000 0x0004
c   0x0002      1 0x0003 0x0000 0x0006
c   0x0002      1 0x0003 0x0002 0x0007
c   0x0000      1 0x0003 0x0002 0x0008
c   0x0000      1 0x0003 0x0002 0x0009
c   0x0000      1 0x0003 0x0002 0x000A
c   0x0000      1 0x0003 0x0002 0x000B
c   0x0000      1 0x0003 0x0002 0x0000
c   0x0000      1 0x0001 0x0002 0x0001
c   0x0000      1 0x0001 0x0000 0x0002
c   0x0001      1 0x0001 0x0000 0x0003
c   0x0001      1 0x0001 0x0000 0x0004
c   0x0001      1 0x0001 0x0000 0x0006
c   0x0001      1 0x0001 0x0001 0x0007
c   0x0000      1 0x0001 0x0001 0x0008
c   0x0000      1 0x0001 0x0001 0x0009
c   0x0000      1 0x0001 0x0001 0x00FF


program(0xb342,0x8443,0xa112,0xb040,0x0d06,0x0500,0x9401,0x0100,0xb024,0x0dff,0x8110,0x0d00)
*/

/* Test case REC:
CLK     R1     R2     R3     R4     PC

0        x      x      x      x 0x0000
c        x      x      x 0x0000 0x0001
c   0x0020      x      x 0x0000 0x0002
c   0x0020 0x0008      x 0x0000 0x0003
c   0x0020 0x0008 0x0001 0x0000 0x0004
c   0x0021 0x0008 0x0001 0x0000 0x0005
c   0x0021 0x0008 0x0001 0xffff 0x0006
c   0x0021 0x0008 0x001f 0xffff 0x0007
c   0x0021 0x0008 0x001f 0xffff 0x0008
c   0x0021 0x0008 0x001f 0xffff 0x0009
c   0x0021 0x0008 0x001f 0xffff 0x000a
c   0x0021 0x0008 0x0001 0xffff 0x000b
c   0x0021 0x0008 0x0001 0xfffe 0x000c
c   0x0021 0x0008 0x0001 0xfffe 0x000d
c   0x000f 0x0008 0x0001 0xfffe 0x000e
c   0x000f 0x0008 0x0001 0xfffd 0x000f
c   0x000f 0x0008 0x0001 0xfffd 0x0010
c   0x000f 0x0007 0x0001 0xfffd 0x0011
c   0xfffe 0x0007 0x0001 0xfffd 0x0012
c   0x0021 0x0007 0x0001 0xfffd 0x0013
c   0x0022 0x0007 0x0001 0xfffd 0x0014
c   0x0022 0x0007 0x0001 0xfffc 0x0015
c   0x0022 0x0007 0x0018 0xfffc 0x0016
c   0x0022 0x0007 0x0018 0xfffc 0x0017
c   0x0022 0x0007 0x0018 0xfffc 0x0008
c   0x0022 0x0007 0x0018 0xfffc 0x0009
c   0x0022 0x0007 0x0018 0xfffc 0x000a
c   0x0022 0x0007 0x0001 0xfffc 0x000b
c   0x0022 0x0007 0x0001 0xfffb 0x000c
c   0x0022 0x0007 0x0001 0xfffb 0x000d
c   0x0004 0x0007 0x0001 0xfffb 0x000e
c   0x0004 0x0007 0x0001 0xfffa 0x000f
c   0x0004 0x0007 0x0001 0xfffa 0x0010
c   0x0004 0x0006 0x0001 0xfffa 0x0011
c   0xfffb 0x0006 0x0001 0xfffa 0x0012
c   0x0022 0x0006 0x0001 0xfffa 0x0013
c   0x0023 0x0006 0x0001 0xfffa 0x0014
c   0x0023 0x0006 0x0001 0xfff9 0x0015
c   0x0023 0x0006 0x0018 0xfff9 0x0016
c   0x0023 0x0006 0x0018 0xfff9 0x0017
c   0x0023 0x0006 0x0018 0xfff9 0x0008
c   0x0023 0x0006 0x0018 0xfff9 0x0009
c   0x0023 0x0006 0x0018 0xfff9 0x000a
c   0x0023 0x0006 0x0001 0xfff9 0x000b
c   0x0023 0x0006 0x0001 0xfff8 0x000c
c   0x0023 0x0006 0x0001 0xfff8 0x000d
c   0x0005 0x0006 0x0001 0xfff8 0x000e
c   0x0005 0x0006 0x0001 0xfff7 0x000f
c   0x0005 0x0006 0x0001 0xfff7 0x0010
c   0x0005 0x0005 0x0001 0xfff7 0x0011
c   0xfff8 0x0005 0x0001 0xfff7 0x0012
c   0x0023 0x0005 0x0001 0xfff7 0x0013
c   0x0024 0x0005 0x0001 0xfff7 0x0014
c   0x0024 0x0005 0x0001 0xfff6 0x0015
c   0x0024 0x0005 0x0018 0xfff6 0x0016
c   0x0024 0x0005 0x0018 0xfff6 0x0017
c   0x0024 0x0005 0x0018 0xfff6 0x0008
c   0x0024 0x0005 0x0018 0xfff6 0x0009
c   0x0024 0x0005 0x0018 0xfff6 0x000a
c   0x0024 0x0005 0x0001 0xfff6 0x000b
c   0x0024 0x0005 0x0001 0xfff5 0x000c
c   0x0024 0x0005 0x0001 0xfff5 0x000d
c   0x0006 0x0005 0x0001 0xfff5 0x000e
c   0x0006 0x0005 0x0001 0xfff4 0x000f
c   0x0006 0x0005 0x0001 0xfff4 0x0010
c   0x0006 0x0004 0x0001 0xfff4 0x0011
c   0xfff5 0x0004 0x0001 0xfff4 0x0012
c   0x0024 0x0004 0x0001 0xfff4 0x0013
c   0x0025 0x0004 0x0001 0xfff4 0x0014
c   0x0025 0x0004 0x0001 0xfff3 0x0015
c   0x0025 0x0004 0x0018 0xfff3 0x0016
c   0x0025 0x0004 0x0018 0xfff3 0x0017
c   0x0025 0x0004 0x0018 0xfff3 0x0008
c   0x0025 0x0004 0x0018 0xfff3 0x0009
c   0x0025 0x0004 0x0018 0xfff3 0x000a
c   0x0025 0x0004 0x0001 0xfff3 0x000b
c   0x0025 0x0004 0x0001 0xfff2 0x000c
c   0x0025 0x0004 0x0001 0xfff2 0x000d
c   0x0007 0x0004 0x0001 0xfff2 0x000e
c   0x0007 0x0004 0x0001 0xfff1 0x000f
c   0x0007 0x0004 0x0001 0xfff1 0x0010
c   0x0007 0x0003 0x0001 0xfff1 0x0011
c   0xfff2 0x0003 0x0001 0xfff1 0x0012
c   0x0025 0x0003 0x0001 0xfff1 0x0013
c   0x0026 0x0003 0x0001 0xfff1 0x0014
c   0x0026 0x0003 0x0001 0xfff0 0x0015
c   0x0026 0x0003 0x0018 0xfff0 0x0016
c   0x0026 0x0003 0x0018 0xfff0 0x0017
c   0x0026 0x0003 0x0018 0xfff0 0x0008
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*/

/* Test case FIB:
CLK     R1     R2     R3     R4   FLAGS     PC

declare FLAGS = FL & 0xF;

0        x      x      x      x      x 0x0000
c   0x0001      x      x      x      x 0x0001
c   0x0001 0x0000      x      x      x 0x0002
c   0x0001 0x0000 0x0019      x      x 0x0003
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*/

/* Test case SETH:
CLK     R1     R2     R3     R4     PC

init R1=0xAD;
init R2=0x0D;
init R3=0xEF;
init R4=0xAD;
0        x      x      x      x 0x0000
c   0xdead 0x000d 0x00ef 0x00ad 0x0001
c   0xdead 0xf00d 0x00ef 0x00ad 0x0002
c   0xdead 0xf00d 0xbeef 0x00ad 0x0003
c   0xdead 0xf00d 0xbeef 0x0bad 0x0004

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*/

/* Test case SETH_PC:
CLK     R1     R2     R3     R4     PC

0        x      x      x      x 0x0000
c   0x0001      x      x      x 0x0001
c   0x0001 0x0002      x      x 0x0002
c   0x0001 0x0002 0x0003      x 0x0003
c   0x0001 0x0002 0x0006      x 0x0004
c   0x0001 0x0002 0x0006      x 0x0104
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*/

/* Test case BUBBLE SORT:
# This test uses a 64-bit key-value pair bubble sort algorithm where comparisons are made only on keys, and key-value relationship remains unchanged.
# For more information, see demo.quac.

	CLK	R2

loop(i, 598)
	c	x
end loop
	c	0x0003
	c	x
	c	0x0064
	c	x
	c	0x006E
	c	x
	c	0x0078
	c	x
	c	0x0028
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*/

/* Test case BASE-OFFSET:
# This tests base+offset immediate operations.
# Assembly: unit_tests/base_offset.quac
	CLK	R1	R2	R3	R4

loop(i, 24)
	c	x	x	x	x	#Don't care about intermediate steps
end loop

	c	(3)	x	(4)	(5)

loop(i, 21)
	c	x	x	x	x	
end loop
	c	(0)	(0x2B)	(7)	(0x1B)

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*/
