// Digital circuit extended_cu.dig as structural Verilog
module extended_cu (
  input  [15:0] INST,
  input  COND,
  output [2:0] RS1,
  output [2:0] RS2,
  output [2:0] WS,
  output STR,
  output WE,
  output [1:0] DMUX,
  output LDR,
  output SETH,
  output [2:0] RS3,
  output [15:0] IMM,
  output PSTO,
  output FLEN,
  output [1:0] ALUOP,
  output WE2,
  output MEMIM,
  output CALREG,
  output CALL,
  output ALUIM,
  output EXEC,
  output SETC
);

  wire and_1_out, and_2_out, and_3_out, and_4_out, and_5_out, and_6_out, and_7_out, and_9_out, and_10_out,
       and_11_out, and_12_out, and_13_out, and_14_out, and_15_out, demultiplexer_1_out_0,
       demultiplexer_1_out_1, demultiplexer_2_out_0, demultiplexer_2_out_1, demultiplexer_3_out_0,
       demultiplexer_3_out_1, demultiplexer_4_out_0, demultiplexer_4_out_1, demultiplexer_5_out_1, LDR_t,
       nor_1_out, nor_2_out, nor_3_out, nor_4_out, nor_5_out, not_1_out, or_2_out, or_5_out, or_8_out,
       or_9_out, or_12_out, or_13_out, RS1_eq_RD, STR_t;
  wire [1:0] multiplexer_2_out, multiplexer_3_out, multiplexer_4_out;
  wire [2:0] multiplexer_6_out;
  wire [15:0] and_16_out, bitextender_1_out, multiplexer_9_out;

  not not_1 (not_1_out, INST[11]);
  or or_1 (EXEC, COND, not_1_out);
  nor nor_1 (nor_1_out, INST[15], INST[14], INST[13]);
  nor nor_2 (nor_2_out, INST[15], INST[13], INST[12]);
  nor nor_3 (nor_3_out, INST[15], INST[14], INST[12]);
  nor nor_4 (nor_4_out, INST[13], INST[12]);
  and and_1 (and_1_out, INST[14], INST[15]);
  and and_2 (and_2_out, nor_1_out, INST[12]);
  and and_3 (and_3_out, ~INST[15], ~INST[14], INST[13], INST[12]);  // And
  and and_4 (and_4_out, ~INST[15], INST[14], INST[13], ~INST[12]);  // And
  and and_5 (and_5_out, ~INST[15], INST[14], ~INST[13], INST[12]);  // And
  and and_6 (and_6_out, ~INST[15], INST[14], INST[13], INST[12]);  // And
  and and_7 (and_7_out, INST[14], nor_2_out);
  nor nor_5 (nor_5_out, INST[15], INST[14], INST[13], INST[12]);
  and and_8 (SETH, INST[13], nor_3_out);
  and and_9 (and_9_out, INST[15], INST[14]);
  and and_10 (and_10_out, INST[15], nor_4_out);
  and and_11 (and_11_out, INST[12], ~INST[13], INST[15]);  // And
  and and_12 (and_12_out, ~INST[12], INST[13], INST[15]);  // And
  and and_13 (and_13_out, INST[12], INST[13], INST[15]);
  Demultiplexer demultiplexer_1 (
    .sel(or_2_out), .in(and_10_out), .out_0(demultiplexer_1_out_0), .out_1(demultiplexer_1_out_1));
  Demultiplexer demultiplexer_2 (
    .sel(or_2_out), .in(and_11_out), .out_0(demultiplexer_2_out_0), .out_1(demultiplexer_2_out_1));
  Demultiplexer demultiplexer_3 (
    .sel(or_2_out), .in(and_12_out), .out_0(demultiplexer_3_out_0), .out_1(demultiplexer_3_out_1));
  Demultiplexer demultiplexer_4 (
    .sel(or_2_out), .in(and_13_out), .out_0(demultiplexer_4_out_0), .out_1(demultiplexer_4_out_1));
  or or_2 (or_2_out, and_1_out, and_14_out);
  and and_14 (and_14_out, ~INST[7], ~INST[3]);  // And
  Demultiplexer demultiplexer_5 (.sel(INST[0]), .in(and_3_out), .out_0(CALREG), .out_1(demultiplexer_5_out_1));
  or or_3 (MEMIM, and_4_out, and_5_out);
  or or_4 (STR_t, and_4_out, and_6_out, CALL, demultiplexer_1_out_0, demultiplexer_2_out_0);
  or or_5 (or_5_out, demultiplexer_1_out_1, demultiplexer_2_out_1, demultiplexer_3_out_1, demultiplexer_4_out_1);
  or or_6 (PSTO, demultiplexer_2_out_0, demultiplexer_4_out_0);
  or or_7 (LDR_t, and_5_out, demultiplexer_3_out_0, demultiplexer_4_out_0, and_7_out);
  or or_8 (or_8_out, nor_5_out, CALL, SETH);
  Multiplexer #(.Bits(2)) multiplexer_1 (.sel(or_5_out), .in_0(2'b10), .in_1(INST[13:12]), .out(ALUOP));
  Multiplexer #(.Bits(2)) multiplexer_2 (.sel(or_8_out), .in_0(2'b00), .in_1(2'b11), .out(multiplexer_2_out));
  Multiplexer #(.Bits(2)) multiplexer_3 (.sel(LDR_t), .in_0(2'b00), .in_1(2'b10), .out(multiplexer_3_out));
  Multiplexer #(.Bits(2)) multiplexer_4 (.sel(or_5_out), .in_0(2'b00), .in_1(2'b01), .out(multiplexer_4_out));
  or or_9 (or_9_out, and_6_out, and_7_out, demultiplexer_1_out_0, PSTO, demultiplexer_3_out_0);
  or or_10 (RS1_eq_RD, SETH, and_9_out);
  Multiplexer #(.Bits(3)) multiplexer_5 (.sel(CALL), .in_0(INST[10:8]), .in_1(3'b101), .out(WS));
  Multiplexer #(.Bits(3)) multiplexer_6 (.sel(RS1_eq_RD), .in_0(INST[6:4]), .in_1(WS), .out(multiplexer_6_out));
  Multiplexer #(.Bits(3)) multiplexer_7 (.sel(CALL), .in_0(INST[2:0]), .in_1(INST[10:8]), .out(RS3));
  Multiplexer #(.Bits(3)) multiplexer_8 (.sel(STR_t), .in_0(INST[2:0]), .in_1(WS), .out(RS2));
  and and_15 (and_15_out, or_9_out, INST[7]);
  Multiplexer #(.Bits(16)) multiplexer_9 (.sel(and_2_out), .in_0(16'hff), .in_1(16'h7ff), .out(multiplexer_9_out));
  assign and_16_out = multiplexer_9_out & INST;  // And and_16, 16 bits wide
  BitExtender #(.inputBits(4)) bitextender_1 (.in(INST[3:0]), .out(bitextender_1_out));
  or or_11 (ALUIM, and_15_out, and_9_out);
  Multiplexer #(.Bits(3)) multiplexer_10 (.sel(CALL), .in_0(multiplexer_6_out), .in_1(3'b110), .out(RS1));
  or or_12 (or_12_out, demultiplexer_1_out_0, PSTO, demultiplexer_3_out_0, CALL);
  and and_17 (SETC, EXEC, demultiplexer_5_out_1);
  Multiplexer #(.Bits(16)) multiplexer_11 (.sel(or_9_out), .in_0(and_16_out), .in_1(bitextender_1_out), .out(IMM));
  or or_13 (or_13_out, ~STR_t, CALL);  // Or
  or or_14 (CALL, and_2_out, CALREG);
  and and_18 (STR, STR_t, EXEC);
  and and_19 (FLEN, or_5_out, EXEC);
  and and_20 (WE, ~SETC, EXEC, or_13_out);  // And
  and and_21 (WE2, EXEC, or_12_out);
  assign DMUX = multiplexer_2_out | multiplexer_3_out | multiplexer_4_out;  // Or or_15, 2 bits wide

  assign LDR = EXEC;

  // Other names for the same wires on the sheet: bit3 = INST[3]; bit7 = INST[7]

  // Notes on the sheet:
  //   IMM: IMM represents the immediate value needed
  //   for various instructions. If the instruction
  //   requries an IMM8, then the last 8 bit is output.
  //   If the instruction requries an IMM4, then the
  //   last four bit is output if the sign bit is 0, otherwise
  //   the 1 is moved to the 15'th bit (this value will be
  //   extended to 16 bits).
  //   PSTO: PSTO stands for "Post-Offset", which is set to true
  //   whenever a post offset LDR or post offset STR instruction
  //   is read.
  //   WE2: ALUIM is set to true whenever an immediate ALU
  //   instruction is input.
  //   MEMIM: MEMIM stands for "memory immediate", which is
  //   switched to true if an immediate LDR/STR
  //   instruction is input.
  //   CALREG: CALREG is true whenever the CALL operation
  //   is detected, but in R-format.
  //   CALL: CALLIM is set to true whenever the immediate 
  //   CALL instruction is input.
  //   ALUIM: ALUIM is set to true whenever an immediate ALU
  //   instruction is input.
  //   opcode
  //   Rd
  //   Ra
  //   Rb
  //   Z
  //   Conditional Execution
  //   Short Operations
  //   ALU Operations
  //   Immediate CALL
  //   SETC, CALL
  //   Memory Operations
  //   Immediate STR (0110)
  //   Immediate LDR (0101)
  //   Condition for 
  //   ALU instruction
  //   STR (0111)
  //   LDR (0100)
  //   MOVL (0000)
  //   SETH (0010)
  //   Pre-Offset STR
  //   Post-Offset STR
  //   Pre-Offset LDR
  //   Post-Offset LDR
  //   SETC
  //   ALU Immediate Operation
  //   CALL
  //   AND (1X00)
  //   ORR (1X01)
  //   ADD (1X10)
  //   SUB (1X11)
  //   Any STR Operation
  //   Any ALU Operations
  //   DMUX Converters
  //   Low immediate line: set to true if imm4 value
  //   Logic for immediate value output:
  //   IMM8 Bitmask:
  //   IMM11 Bitmask:
  //   IMM4 sign extension:
  //   Sign extension
  //   ADDITIONAL TESTS
endmodule

/* Test case Base ISA Tests:
	INST                                    WE  ALUOP  RS1   RS2  WS  STR  LDR DMUX  FLEN

let aluop  = 0b1000;
let ldrop  = 0b0100;
let strop  = 0b0111;
let movlop = 0b0000;

loop(rd, 1<<3)
loop(ra, 1<<3)
loop(rb, 1<<3)

loop(i, 4)
	((aluop+i)<<12 | rd<<8 | ra<<4 | rb<<0) 1  (i)     (ra)  (rb) (rd)  0   X    1    1     #test add/sub/and/orr
end loop

	(ldrop    <<12 | rd<<8 | ra<<4 )        1  X       (ra)  x    (rd)  0   1    2    0     #test ldr
	(strop    <<12 | rd<<8 | ra<<4 )        0  X       (ra)  (rd)  X    1   X    X    0     #test str
	
	let imm = random(256);
	(movlop   <<12 | rd<<8 | imm )          1  X       X      X   (rd)  0   X    3    0     #test movl

end loop
end loop
end loop
*/

/* Test case WS:
	INST                                    WS 

let aluop  = 0b1000;
let ldrop  = 0b0100;
let strop  = 0b0111;
let movlop = 0b0000;

loop(rd, 1<<3)
loop(ra, 1<<3)
loop(rb, 1<<3)

loop(i, 4)
	((aluop+i)<<12 | rd<<8 | ra<<4 | rb<<0) (rd)  #test add/sub/and/orr
end loop

	(ldrop    <<12 | rd<<8 | ra<<4 )        (rd)   #test ldr
	(strop    <<12 | rd<<8 | ra<<4 )        X     #test str
	
	let imm = random(256);
	(movlop   <<12 | rd<<8 | imm )          (rd)  #test movl

end loop
end loop
end loop
*/

/* Test case RS1:
	INST                                    RS1  

let aluop  = 0b1000;
let ldrop  = 0b0100;
let strop  = 0b0111;
let movlop = 0b0000;

loop(rd, 1<<3)
loop(ra, 1<<3)
loop(rb, 1<<3)

loop(i, 4)
	((aluop+i)<<12 | rd<<8 | ra<<4 | rb<<0) (ra)  #test add/sub/and/orr
end loop

	(ldrop    <<12 | rd<<8 | ra<<4 )        (ra)  #test ldr
	(strop    <<12 | rd<<8 | ra<<4 )        (ra)  #test str

end loop
end loop
end loop
*/

/* Test case RS2:
	INST                                    RS2  

let aluop  = 0b1000;
let ldrop  = 0b0100;
let strop  = 0b0111;
let movlop = 0b0000;

loop(rd, 1<<3)
loop(ra, 1<<3)
loop(rb, 1<<3)

loop(i, 4)
	((aluop+i)<<12 | rd<<8 | ra<<4 | rb<<0) (rb) #test add/sub/and/orr
end loop
	(strop    <<12 | rd<<8 | ra<<4 )        (rd) #test str

end loop
end loop
end loop
*/

/* Test case STR:
	INST                                    STR 

let aluop  = 0b1000;
let ldrop  = 0b0100;
let strop  = 0b0111;
let movlop = 0b0000;

loop(rd, 1<<3)
loop(ra, 1<<3)
loop(rb, 1<<3)

loop(i, 4)
	((aluop+i)<<12 | rd<<8 | ra<<4 | rb<<0) 0  #test add/sub/and/orr
end loop

	(ldrop    <<12 | rd<<8 | ra<<4 )        0  #test ldr
	(strop    <<12 | rd<<8 | ra<<4 )        1  #test str
	
	let imm = random(256);
	(movlop   <<12 | rd<<8 | imm )          0  #test movl

end loop
end loop
end loop
*/

/* Test case WE:
	INST                                    WE  

let aluop  = 0b1000;
let ldrop  = 0b0100;
let strop  = 0b0111;
let movlop = 0b0000;

loop(rd, 1<<3)
loop(ra, 1<<3)
loop(rb, 1<<3)

loop(i, 4)
	((aluop+i)<<12 | rd<<8 | ra<<4 | rb<<0) 1  #test add/sub/and/orr
end loop

	(ldrop    <<12 | rd<<8 | ra<<4 )        1  #test ldr
	(strop    <<12 | rd<<8 | ra<<4 )        0  #test str
	
	let imm = random(256);
	(movlop   <<12 | rd<<8 | imm )          1  #test movl

end loop
end loop
end loop
*/

/* Test case LDR:
	INST                                    LDR 

let aluop  = 0b1000;
let ldrop  = 0b0100;
let strop  = 0b0111;
let movlop = 0b0000;

loop(rd, 1<<3)
loop(ra, 1<<3)
loop(rb, 1<<3)

loop(i, 4)
	((aluop+i)<<12 | rd<<8 | ra<<4 | rb<<0) X    #test add/sub/and/orr
end loop

	(ldrop    <<12 | rd<<8 | ra<<4 )        1    #test ldr
	(strop    <<12 | rd<<8 | ra<<4 )        X    #test str
	
	let imm = random(256);
	(movlop   <<12 | rd<<8 | imm )          X    #test movl

end loop
end loop
end loop
*/

/* Test case DMUX:
	INST                                    DMUX

let aluop  = 0b1000;
let ldrop  = 0b0100;
let strop  = 0b0111;
let movlop = 0b0000;

loop(rd, 1<<3)
loop(ra, 1<<3)
loop(rb, 1<<3)

loop(i, 4)
	((aluop+i)<<12 | rd<<8 | ra<<4 | rb<<0) 1  #test add/sub/and/orr
end loop

	(ldrop    <<12 | rd<<8 | ra<<4 )        2  #test ldr
	
	let imm = random(256);
	(movlop   <<12 | rd<<8 | imm )          3  #test movl

end loop
end loop
end loop
*/

/* Test case ALUOP:
	INST                                    ALUOP 

let aluop  = 0b1000;
let ldrop  = 0b0100;
let strop  = 0b0111;
let movlop = 0b0000;

loop(rd, 1<<3)
loop(ra, 1<<3)
loop(rb, 1<<3)

loop(i, 4)
	((aluop+i)<<12 | rd<<8 | ra<<4 | rb<<0) (i)    #test add/sub/and/orr
end loop

end loop
end loop
end loop
*/

/* Test case FLEN:
	INST                                    FLEN 

let aluop  = 0b1000;
let ldrop  = 0b0100;
let strop  = 0b0111;
let movlop = 0b0000;

loop(rd, 1<<3)
loop(ra, 1<<3)
loop(rb, 1<<3)

loop(i, 4)
	((aluop+i)<<12 | rd<<8 | ra<<4 | rb<<0) (1)    #test add/sub/and/orr
	((aluop+i)<<12 | rd<<8 | 1<<7| ra<<4 | rb<<0) (0)    #test pre/post STR, LDR
	((aluop+i)<<12 | rd<<8 | ra<<4 | 1<<3 | rb<<0) (0)    #test pre/post STR, LDR
end loop
end loop
end loop
end loop
*/

/* Test case SETH:
	INST                              SETH 
let aluop  = 0b1000;
let ldrop  = 0b0100;
let strop  = 0b0111;
let movlop = 0b0000;

loop(rd, 1<<3)
loop(ra, 1<<3)
loop(rb, 1<<3)
	#SETH should only be set to true when opcode = 1
	(0<<12| rd<<8 | ra<<4 | rb<<0)    (0) 
	(1<<12| rd<<8 | ra<<4 | rb<<0)    (0) 
	(2<<12| rd<<8 | ra<<4 | rb<<0)    (1) 
loop(i, 13)
	((i+3)<<12|rd<<8 | ra<<4 | rb<<0) (0) 
end loop
end loop
end loop
end loop
*/

/* Test case EXEC:
	INST		COND	EXEC	WE	SETC	WE2	FLEN
loop(o, 16)
loop(x, 1024)
	(o<<12|0<<11|x)	(0)	(1)	X	X	X	X
	(o<<12|0<<11|x)	(1)	(1)	X	X	X	X
	(o<<12|1<<11|x)	(0)	(0)	(0)	(0)	(0)	(0)
	(o<<12|1<<11|x)	(1)	(1)	X	X	X	X
end loop
end loop
*/

/* Test case ALUIM:
	INST                                    ALUIM 

let aluop  = 0b1000;
let aluopim  = 0b1100;
let bad1  = 0b0000;
let bad2  = 0b0100;

loop(rd, 1<<3)
loop(ra, 1<<3)
loop(rb, 1<<3)

loop(i, 4)
	((aluop+i)<<12 | rd<<8 | ra<<4 | rb<<0)   (0) 
	((aluopim+i)<<12 | rd<<8 | ra<<4 | rb<<0) (1) 
	((bad1+i)<<12 | rd<<8 | ra<<4 | rb<<0)    (0) 
	((bad2+i)<<12 | rd<<8 | ra<<4 | rb<<0)    (0)    
end loop

end loop
end loop
end loop
*/

/* Test case PSTO:
	INST                                     PSTO 

let postSTR  = 0b1001;
let postLDR = 0b1011;

loop(rd, 1<<3)
loop(ra, 1<<3)
loop(rb, 1<<3)
	(postSTR<<12|rd<<8|0<<7|ra<<4|1<<3|rb)	 (1)
	(postLDR<<12|rd<<8|0<<7|ra<<4|1<<3|rb)	 (1)
	(postSTR<<12|rd<<8|1<<7|ra<<4|1<<3|rb)	 (1)
	(postLDR<<12|rd<<8|1<<7|ra<<4|1<<3|rb)	 (1)
	(postSTR<<12|rd<<8|1<<7|ra<<4|0<<3|rb)	 (1)
	(postLDR<<12|rd<<8|1<<7|ra<<4|0<<3|rb)	 (1)
	(postSTR<<12|rd<<8|0<<7|ra<<4|0<<3|rb)	 (0)
	(postLDR<<12|rd<<8|0<<7|ra<<4|0<<3|rb)	 (0)
end loop
end loop
end loop
*/

/* Test case SETC:
	INST                   SETC 

let setc  = 0b0011;

loop(rd, 1<<3)
	(setc<<12|rd<<8|1)	(1)
	(setc<<12|rd<<8|0)	(0)
end loop
*/

/* Test case CALL:
	INST                        CALL 	CALREG

let callop  = 0b0001;
let shortop  = 0b0011;

loop(rd, 1<<3)
	(shortop<<12 | rd<<8 | 0)   (1)  	(1)
	(shortop<<12 | rd<<8 | 1)   (0)  	(0)
end loop

loop(imm, 1<<11)	
	(callop<<12 | imm)	    (1)		(0)
end loop
*/

/* Test case STR_extended:
	INST                                    	STR 
# Tests the STR line for Pre/Post Offset
let prestr = 0b1000;
let poststr = 0b1001;

loop(rd, 1<<3)
loop(ra, 1<<3)
loop(rb, 1<<3)
	(prestr << 12 | rd<<8 | ra<<4 | 1<<3 | rb)    (1)
	(poststr << 12 | rd<<8 | ra<<4 | 1<<3 | rb)   (1)
end loop
loop(imm, 1<<4)
	(prestr << 12 | rd<<8 | 1<<7 | ra<<4 | imm)    	(1)
	(poststr << 12 | rd<<8 | 1<<7 | ra<<4 | imm)   	(1)
end loop
end loop
end loop
*/

/* Test case LDR_extended:
	INST                                    	LDR 
# Tests the STR line for Pre/Post Offset
let preldr = 0b1010;
let postldr = 0b1011;

loop(rd, 1<<3)
loop(ra, 1<<3)
loop(rb, 1<<3)
	(preldr << 12 | rd<<8 | ra<<4 | 1<<3 | rb)    (1)
	(postldr << 12 | rd<<8 | ra<<4 | 1<<3 | rb)   (1)
end loop
loop(imm, 1<<4)
	(preldr << 12 | rd<<8 | 1<<7 | ra<<4 | imm)    	(1)
	(postldr << 12 | rd<<8 | 1<<7 | ra<<4 | imm)   	(1)
end loop
end loop
end loop
*/

/* Test case IMM_8:
	INST                 	 IMM 
# Tests imm8 
let movl = 0b0000 << 12;
let seth = 0b0010 << 12;
let and = 0b1100 << 12;
let orr = 0b1101 << 12;
let add = 0b1110 << 12;
let sub = 0b1111 << 12;

loop(rd, 1<<3)
loop(imm, 1<<8)
	(movl|rd<<8|imm)	(imm)
	(seth|rd<<8|imm)	(imm)
	(and|rd<<8|imm)		(imm)
	(orr|rd<<8|imm)		(imm)
	(add|rd<<8|imm)		(imm)
	(sub|rd<<8|imm)		(imm)
end loop
end loop
*/

/* Test case IMM_11:
	INST                 	 IMM 
# Tests imm11 
let call = 0b0001 << 12;

loop(imm, 1<<11)
	(call|imm)		(imm)
end loop
*/

/* Test case IMM_4:
	INST                 	 		IMM 
# Tests imm4 and its sign extension
let ldr = 0b0100 << 12;
let str = 0b0111 << 12;
let prestr = 0b1000 << 12;
let poststr = 0b1001 << 12;
let preldr = 0b1010 << 12;
let postldr = 0b1011 << 12;

loop(rd, 1<<3)
loop(ra, 1<<3)
loop(imm, 1<<3) #Sign bit = 0
	(ldr|rd<<8|1<<7|ra<<4|imm)		(imm)
	(str|rd<<8|1<<7|ra<<4|imm)		(imm)
	(prestr|rd<<8|1<<7|ra<<4|imm)		(imm)
	(poststr|rd<<8|1<<7|ra<<4|imm)		(imm)
	(preldr|rd<<8|1<<7|ra<<4|imm)		(imm)
	(postldr|rd<<8|1<<7|ra<<4|imm)		(imm)
end loop

loop(imm, 1<<3) #Sign bit = 1
	(ldr|rd<<8|1<<7|ra<<4|1<<3|imm)		(0b1111111111111<<3|imm)
	(str|rd<<8|1<<7|ra<<4|1<<3|imm)		(0b1111111111111<<3|imm)
	(prestr|rd<<8|1<<7|ra<<4|1<<3|imm)	(0b1111111111111<<3|imm)
	(poststr|rd<<8|1<<7|ra<<4|1<<3|imm)	(0b1111111111111<<3|imm)
	(preldr|rd<<8|1<<7|ra<<4|1<<3|imm)	(0b1111111111111<<3|imm)
	(postldr|rd<<8|1<<7|ra<<4|1<<3|imm)	(0b1111111111111<<3|imm)
end loop

end loop
end loop
*/

/* Test case MEMIM:
	INST			MEMIM
let immldr = 0b0101 << 12;
let immstr = 0b0110 << 12;

loop(rd, 1<<3)
loop(imm, 1<<8)
	(immldr|rd<<8|imm)	(1)
	(immstr|rd<<8|imm)	(1)
end loop
end loop
*/
