// Digital circuit extended_regfile.dig as structural Verilog
module extended_regfile (
  input  [2:0] RS1,
  input  [2:0] RS2,
  input  WE1,
  input  [15:0] IN1,
  input  clk,
  input  [2:0] WS1,
  input  [2:0] RS3,
  input  [2:0] WS2,
  input  [15:0] IN2,
  input  PRI,
  input  WE2,
  input  [3:0] FLD,
  input  FLEN,
  output [15:0] OUT1,
  output [15:0] OUT2,
  output [15:0] PC,
  output [15:0] OUT3,
  output [15:0] PC_plus_1,
  output [15:0] FL
);

  wire demultiplexer_1_out_1, demultiplexer_1_out_2, demultiplexer_1_out_3, demultiplexer_1_out_4,
       demultiplexer_1_out_5, demultiplexer_1_out_6, demultiplexer_2_out_1, demultiplexer_2_out_2,
       demultiplexer_2_out_3, demultiplexer_2_out_4, demultiplexer_2_out_5, demultiplexer_2_out_6, or_1_out,
       or_2_out, or_3_out, or_4_out, or_5_out, or_6_out;
  wire [15:0] demultiplexer_3_out_1, demultiplexer_3_out_2, demultiplexer_3_out_3, demultiplexer_3_out_4,
       demultiplexer_3_out_5, demultiplexer_3_out_6, demultiplexer_4_out_1, demultiplexer_4_out_2,
       demultiplexer_4_out_3, demultiplexer_4_out_4, demultiplexer_4_out_5, demultiplexer_4_out_6,
       multiplexer_1_out, priority_selector_1_out, priority_selector_2_out, priority_selector_3_out,
       priority_selector_4_out, priority_selector_5_out, priority_selector_6_out, R1_q, R2_q, R3_q, R4_q,
       SP_q;

  Demultiplexer #(.Selector_Bits(3)) demultiplexer_1 (
    .sel(WS2), .in(WE2), .out_1(demultiplexer_1_out_1), .out_2(demultiplexer_1_out_2),
    .out_3(demultiplexer_1_out_3), .out_4(demultiplexer_1_out_4), .out_5(demultiplexer_1_out_5),
    .out_6(demultiplexer_1_out_6));  // open: out_0, out_7
  Demultiplexer #(.Selector_Bits(3)) demultiplexer_2 (
    .sel(WS1), .in(WE1), .out_1(demultiplexer_2_out_1), .out_2(demultiplexer_2_out_2),
    .out_3(demultiplexer_2_out_3), .out_4(demultiplexer_2_out_4), .out_5(demultiplexer_2_out_5),
    .out_6(demultiplexer_2_out_6));  // open: out_0, out_7
  Demultiplexer #(.Selector_Bits(3), .Bits(16)) demultiplexer_3 (
    .sel(WS1), .in(IN1), .out_1(demultiplexer_3_out_1), .out_2(demultiplexer_3_out_2),
    .out_3(demultiplexer_3_out_3), .out_4(demultiplexer_3_out_4), .out_5(demultiplexer_3_out_5),
    .out_6(demultiplexer_3_out_6));  // open: out_0, out_7
  Demultiplexer #(.Selector_Bits(3), .Bits(16)) demultiplexer_4 (
    .sel(WS2), .in(IN2), .out_1(demultiplexer_4_out_1), .out_2(demultiplexer_4_out_2),
    .out_3(demultiplexer_4_out_3), .out_4(demultiplexer_4_out_4), .out_5(demultiplexer_4_out_5),
    .out_6(demultiplexer_4_out_6));  // open: out_0, out_7
  priority_selector priority_selector_1 (
    .IN2(demultiplexer_4_out_5), .IN1(demultiplexer_3_out_5), .PRI(PRI), .EN2(demultiplexer_1_out_5),
    .EN1(demultiplexer_2_out_5), .OUT(priority_selector_1_out));
  or or_1 (or_1_out, demultiplexer_2_out_5, demultiplexer_1_out_5);
  priority_selector priority_selector_2 (
    .IN2(demultiplexer_4_out_1), .IN1(demultiplexer_3_out_1), .PRI(PRI), .EN2(demultiplexer_1_out_1),
    .EN1(demultiplexer_2_out_1), .OUT(priority_selector_2_out));
  or or_2 (or_2_out, demultiplexer_2_out_1, demultiplexer_1_out_1);
  priority_selector priority_selector_3 (
    .IN2(demultiplexer_4_out_2), .IN1(demultiplexer_3_out_2), .PRI(PRI), .EN2(demultiplexer_1_out_2),
    .EN1(demultiplexer_2_out_2), .OUT(priority_selector_3_out));
  or or_3 (or_3_out, demultiplexer_2_out_2, demultiplexer_1_out_2);
  priority_selector priority_selector_4 (
    .IN2(demultiplexer_4_out_3), .IN1(demultiplexer_3_out_3), .PRI(PRI), .EN2(demultiplexer_1_out_3),
    .EN1(demultiplexer_2_out_3), .OUT(priority_selector_4_out));
  or or_4 (or_4_out, demultiplexer_2_out_3, demultiplexer_1_out_3);
  priority_selector priority_selector_5 (
    .IN2(demultiplexer_4_out_4), .IN1(demultiplexer_3_out_4), .PRI(PRI), .EN2(demultiplexer_1_out_4),
    .EN1(demultiplexer_2_out_4), .OUT(priority_selector_5_out));
  or or_5 (or_5_out, demultiplexer_2_out_4, demultiplexer_1_out_4);
  priority_selector priority_selector_6 (
    .IN2(demultiplexer_4_out_6), .IN1(demultiplexer_3_out_6), .PRI(PRI), .EN2(demultiplexer_1_out_6),
    .EN1(demultiplexer_2_out_6), .OUT(priority_selector_6_out));
  or or_6 (or_6_out, demultiplexer_2_out_6, demultiplexer_1_out_6);
  Multiplexer #(.Bits(16)) multiplexer_1 (
    .sel(or_1_out), .in_0(PC_plus_1), .in_1(priority_selector_1_out), .out(multiplexer_1_out));
  Register #(.Bits(16)) R1 (.D(priority_selector_2_out), .C(clk), .en(or_2_out), .Q(R1_q));
  Register #(.Bits(16)) R2 (.D(priority_selector_3_out), .C(clk), .en(or_3_out), .Q(R2_q));
  Register #(.Bits(16)) R3 (.D(priority_selector_4_out), .C(clk), .en(or_4_out), .Q(R3_q));
  Register #(.Bits(16)) R4 (.D(priority_selector_5_out), .C(clk), .en(or_5_out), .Q(R4_q));
  Register #(.Bits(16), .isProgramCounter("true")) u_PC (.D(multiplexer_1_out), .C(clk), .en(1'b1), .Q(PC));
  Add #(.Bits(16)) plus_1 (.a(16'h1), .b(PC), .c_i(1'b0), .s(PC_plus_1));  // open: c_o
  Register #(.Bits(16)) SP (.D(priority_selector_6_out), .C(clk), .en(or_6_out), .Q(SP_q));
  Register #(.Bits(16)) u_FL (.D({{12{1'b0}}, FLD}), .C(clk), .en(FLEN), .Q(FL));
  Multiplexer #(.Selector_Bits(3), .Bits(16)) multiplexer_2 (
    .sel(RS1), .in_0({16{1'b0}}), .in_1(R1_q), .in_2(R2_q), .in_3(R3_q), .in_4(R4_q), .in_5(PC), .in_6(SP_q),
    .in_7(FL), .out(OUT1));
  Multiplexer #(.Selector_Bits(3), .Bits(16)) multiplexer_3 (
    .sel(RS2), .in_0({16{1'b0}}), .in_1(R1_q), .in_2(R2_q), .in_3(R3_q), .in_4(R4_q), .in_5(PC), .in_6(SP_q),
    .in_7(FL), .out(OUT2));
  Multiplexer #(.Selector_Bits(3), .Bits(16)) multiplexer_4 (
    .sel(RS3), .in_0({16{1'b0}}), .in_1(R1_q), .in_2(R2_q), .in_3(R3_q), .in_4(R4_q), .in_5(PC), .in_6(SP_q),
    .in_7(FL), .out(OUT3));

  // Notes on the sheet:
  //   RS1: The index of the register which should output its value to OUT1.
  //   RS2: The index of the register which should output its value to OUT2.
  //   WE1: Whether the register selected by WS should save the value from IN on the next cycle.
  //   IN1: The value to be saved into the register specified by WS if WE is high,
  //   OUT1: The value in the register specified by RS1.
  //   OUT2: The value in the register specified by RS2.
  //   WS1: The index of the register which should save the value on IN on the next clock cycle (if WE is high).
  //   OUT3: The value in the register specified by RS2.
  //   RS3: The index of the register which should output its value to OUT2.
  //   IN2: The value to be saved into the register specified by WS if WE is high,
  //   PRI: PRI stands for the input priority in case when
  //   both ports attempt to write to the same register.
  //   WE2: Whether the register selected by WS should save the value from IN on the next cycle.
endmodule

/* Test case Single Port Test:
clk PRI WS2 IN2 RS1 RS2 WS1 WE1 WE2 IN1 OUT1 OUT2
c 0 0 0x0000 0 0 0 1 0 0x1234 0x0000 0x0000
c 0 0 0x0000 1 0 1 1 0 0xBEEF 0xBEEF 0x0000
c 0 0 0x0000 2 1 2 1 0 0xDEAD 0xDEAD 0xBEEF
c 0 0 0x0000 3 2 3 1 0 0xFFFF 0xFFFF 0xDEAD
c 0 0 0x0000 3 2 3 0 0 0xABCD 0xFFFF 0xDEAD
c 0 0 0x0000 3 2 2 0 0 0xABCD 0xFFFF 0xDEAD
c 0 0 0x0000 1 0 1 0 0 0xABCD 0xBEEF 0x0000
c 0 0 0x0000 1 0 0 0 0 0xABCD 0xBEEF 0x0000
c 0 0 0x0000 1 0 2 1 0 0xBADE 0xBEEF 0x0000
c 0 0 0x0000 0 2 2 1 0 0xBADE 0x0000 0xBADE
c 0 0 0x0000 0 0 2 0 0 0x1234 0x0000 0x0000
c 0 0 0x0000 2 3 0 1 0 0x0000 0xBADE 0xFFFF
c 0 0 0x0000 0 0 2 0 0 0x1234 0x0000 0x0000
*/

/* Test case Dual Port Test:
clk PRI WS1 WS2 IN1     IN2     WE1 WE2  RS1 RS2 OUT1    OUT2
c   1   1   2   0xABCD  0x1234  1   1	1   2   0xABCD  0x1234
c   1   3   3   0x1111  0x2222  1   1	1   3   0xABCD  0x2222
c   1   4   4   0x0101  0x0202  1   1	3   4   0x2222  0x0202
c   1   1   3   0x0000  0x0345  1   1	1   3   0x0000  0x0345
c   1   1   1   0x0000  0x9999  1   1	1   1   0x9999  0x9999
c   0   1   2   0x1111  0x2222  1   1	1   2   0x1111  0x2222
c   0   3   4   0x3333  0x4444  1   1	1   2   0x1111  0x2222
c   0   1   1   0xAACA  0xCCBC  1   1	3   4   0x3333  0x4444
c   0   0   0   0xAACA  0xCCBC  1   1	1   1   0xAACA  0xAACA
c   0   2   2   0x0000  0xFFFF  1   1	4   2   0x4444  0x0000
c   0   1   1   0x0000  0xFFFF  1   1	4   1   0x4444  0x0000
c   0   3   3   0x0000  0xFFFF  1   1	4   3   0x4444  0x0000
c   0   4   4   0x0000  0xFFFF  1   1	4   3   0x0000  0x0000
c   1   2   2   0x0000  0xFFFF  1   1	4   2   0x0000  0xFFFF
c   1   1   1   0x0000  0xFFFF  1   1	4   1   0x0000  0xFFFF
c   1   3   3   0x0000  0xFFFF  1   1	4   3   0x0000  0xFFFF
c   1   4   4   0x0000  0xFFFF  1   1	4   3   0xFFFF  0xFFFF
c   1   2   2   0x69A3  0x8BC2  1   1	2   1   0x8BC2  0xFFFF
c   1   2   2   0x0001  0x0002  1   0	2   2   0x0001  0x0001
c   1   1   1   0xABCD  0x0ECD  0   1	0   1   0x0000  0x0ECD
*/
