// Digital circuit priority_selector.dig as structural Verilog
// Accepts two 16-bit inputs, if one
// is zero, output the non-zero input.
// If both are non-zero, the second
// input takes precedence.
module priority_selector (
  input  [15:0] IN2,
  input  [15:0] IN1,
  input  PRI,
  input  EN2,
  input  EN1,
  output [15:0] OUT
);

  wire [15:0] multiplexer_1_out;

  Multiplexer #(.Bits(16)) multiplexer_1 (.sel(PRI), .in_0(IN1), .in_1(IN2), .out(multiplexer_1_out));
  Multiplexer #(.Bits(16), .Selector_Bits(2)) multiplexer_2 (
    .sel({EN2, EN1}), .in_0({16{1'b0}}), .in_1(IN1), .in_2(IN2), .in_3(multiplexer_1_out), .out(OUT));

  // Notes on the sheet:
  //   This component accepts two 16-bit
  //   inputs, and enable lines respectively.
  //   This is used in the dual port register file
  //   to choose which input to let in the write port
  //   of a register. If both EN1 and EN2 are on,
  //   then input 2 takes precedence if PRI is set to 1,
  //   otherwise input 1 takes precedence. If only
  //   one is set to true, the associated input
  //   will be output unmodified. If both enable
  //   lines are 0, then the behaviour remains
  //   undefined.
endmodule

/* Test case:
IN1	IN2	PRI EN1 EN2 OUT
0x0000  0x0000  1   0   0   0x0000
0x0000  0xAAAA  1   0   1   0xAAAA
0xABCD  0x0000  1   1   0   0xABCD
0x0000  0x0000  0   0   0   0x0000
0x0000  0xAAAA  0   0   1   0xAAAA
0xABCD  0x0000  0   1   0   0xABCD
0x1234  0xABCD  1   1   1   0xABCD
0x1234  0xABCD  0   1   1   0x1234

0xABCD 0x1234   1   1   1   0x1234
0x3030 0xD0E0   0   1   1   0x3030
*/
