// Digital circuit reg_file.dig as structural Verilog
module reg_file (
  input  [2:0] RS1,
  input  [2:0] RS2,
  input  WE,
  input  [15:0] IN,
  input  clk,
  input  [2:0] WS,
  input  [3:0] FLD,
  input  FLEN,
  output [15:0] OUT1,
  output [15:0] OUT2,
  output [15:0] PC,
  output [15:0] FL
);

  wire demultiplexer_1_out_1, demultiplexer_1_out_2, demultiplexer_1_out_3, demultiplexer_1_out_4,
       demultiplexer_1_out_5;
  wire [15:0] demultiplexer_2_out_1, demultiplexer_2_out_2, demultiplexer_2_out_3, demultiplexer_2_out_4,
       demultiplexer_2_out_5, multiplexer_1_out, plus_1_s, R1_q, R2_q, R3_q, R4_q;

  Demultiplexer #(.Selector_Bits(3)) demultiplexer_1 (
    .sel(WS), .in(WE), .out_1(demultiplexer_1_out_1), .out_2(demultiplexer_1_out_2),
    .out_3(demultiplexer_1_out_3), .out_4(demultiplexer_1_out_4), .out_5(demultiplexer_1_out_5));  // open: out_0, out_6, out_7
  Demultiplexer #(.Selector_Bits(3), .Bits(16)) demultiplexer_2 (
    .sel(WS), .in(IN), .out_1(demultiplexer_2_out_1), .out_2(demultiplexer_2_out_2),
    .out_3(demultiplexer_2_out_3), .out_4(demultiplexer_2_out_4), .out_5(demultiplexer_2_out_5));  // open: out_0, out_6, out_7
  Multiplexer #(.Bits(16)) multiplexer_1 (
    .sel(demultiplexer_1_out_5), .in_0(plus_1_s), .in_1(demultiplexer_2_out_5), .out(multiplexer_1_out));
  Register #(.Bits(16)) R1 (.D(demultiplexer_2_out_1), .C(clk), .en(demultiplexer_1_out_1), .Q(R1_q));
  Register #(.Bits(16)) R2 (.D(demultiplexer_2_out_2), .C(clk), .en(demultiplexer_1_out_2), .Q(R2_q));
  Register #(.Bits(16)) R3 (.D(demultiplexer_2_out_3), .C(clk), .en(demultiplexer_1_out_3), .Q(R3_q));
  Register #(.Bits(16)) R4 (.D(demultiplexer_2_out_4), .C(clk), .en(demultiplexer_1_out_4), .Q(R4_q));
  Register #(.Bits(16), .isProgramCounter("true")) u_PC (.D(multiplexer_1_out), .C(clk), .en(1'b1), .Q(PC));
  Add #(.Bits(16)) plus_1 (.a(16'h1), .b(PC), .c_i(1'b0), .s(plus_1_s));  // open: c_o
  Register #(.Bits(16)) u_FL (.D({{12{1'b0}}, FLD}), .C(clk), .en(FLEN), .Q(FL));
  Multiplexer #(.Selector_Bits(3), .Bits(16)) multiplexer_2 (
    .sel(RS1), .in_0({16{1'b0}}), .in_1(R1_q), .in_2(R2_q), .in_3(R3_q), .in_4(R4_q), .in_5(PC),
    .in_6({16{1'b0}}), .in_7(FL), .out(OUT1));
  Multiplexer #(.Selector_Bits(3), .Bits(16)) multiplexer_3 (
    .sel(RS2), .in_0({16{1'b0}}), .in_1(R1_q), .in_2(R2_q), .in_3(R3_q), .in_4(R4_q), .in_5(PC),
    .in_6({16{1'b0}}), .in_7(FL), .out(OUT2));

  // Notes on the sheet:
  //   RS1: The index of the register which should output its value to OUT1.
  //   RS2: The index of the register which should output its value to OUT2.
  //   WE: Whether the register selected by WS should save the value from IN on the next cycle.
  //   IN: The value to be saved into the register specified by WS if WE is high,
  //   OUT1: The value in the register specified by RS1.
  //   OUT2: The value in the register specified by RS2.
  //   WS: The index of the register which should save the value on IN on the next clock cycle (if WE is high).
endmodule

/* Test case:
clk RS1 RS2 WS WE IN OUT1 OUT2
c 0 0 0 1 0x1234 0x0000 0x0000
c 1 0 1 1 0xBEEF 0xBEEF 0x0000
c 2 1 2 1 0xDEAD 0xDEAD 0xBEEF
c 3 2 3 1 0xFFFF 0xFFFF 0xDEAD
c 3 2 3 0 0xABCD 0xFFFF 0xDEAD
c 3 2 2 0 0xABCD 0xFFFF 0xDEAD
c 1 0 1 0 0xABCD 0xBEEF 0x0000
c 1 0 0 0 0xABCD 0xBEEF 0x0000
c 1 0 2 1 0xBADE 0xBEEF 0x0000
c 0 2 2 1 0xBADE 0x0000 0xBADE
c 0 0 2 0 0x1234 0x0000 0x0000
c 2 3 0 1 0x0000 0xBADE 0xFFFF
c 0 0 2 0 0x1234 0x0000 0x0000
*/
